# Fritzing sketch sketch (saved by Fritzing 0.8.3b)
breadboards: 1

parts:
  U5 = mystery part, 3 pins [chip_label=DS18B20 spacing=300mil]  # not connected
  R5 = Resistor [tolerance=±5% resistance=4.7k package=THT]
  Часть1 = DeuLigne 1.1 - The Snootlab's LCD shield for Arduino
  U6 = BLUETOOTH-RN41 [package=rn41]  # not connected

nets:
  N1: R5.Pin_0, Часть1.+5V
